// Logisim project Desafio 1.circ as structural Verilog: 1 circuit, main circuit main
module main (
  input  X1,
  input  X2,
  input  X3
);

  wire and_1_out, not_1_out, not_2_out, not_3_out, or_1_out;

  not not_1 (not_1_out, X1);
  not not_2 (not_2_out, X2);
  and and_1 (and_1_out, not_2_out, X3);
  or or_1 (or_1_out, not_1_out, and_1_out);
  not not_3 (not_3_out, or_1_out);
  LED led_1 (.in(not_3_out));

  // Notes on the sheet:
  //   Resposta: Alternativa B
  //   S1
  //   S2
  //   S
  //   S2 = X3 . X2'
  //   S=(S1+S2)'
  //   S= (X3.(X2)' +X1)'
endmodule
