// Logisim project Desafio 2.circ as structural Verilog: 1 circuit, main circuit main
module main (
  input  Ta,
  input  Ta_2,
  input  Tb,
  input  Tb_2,
  input  Tc,
  input  Tc_2,
  input  Ta_3,
  input  Tb_3,
  input  Tc_3
);

  wire and_1_out, and_2_out, and_3_out, and_4_out, and_5_out, and_6_out, or_1_out, or_2_out, or_3_out;

  and and_1 (and_1_out, Ta_2, Tb_2);
  and and_2 (and_2_out, Tb_2, Tc_2);
  and and_3 (and_3_out, Ta_3, Tb_3);
  and and_4 (and_4_out, Tb_3, Tc_3);
  LED led_1 (.in(or_1_out));
  or or_1 (or_1_out, and_1_out, and_2_out);
  LED led_2 (.in(or_2_out));
  or or_2 (or_2_out, and_3_out, and_4_out);
  and and_5 (and_5_out, Ta, Tb);
  and and_6 (and_6_out, Tb, Tc);
  or or_3 (or_3_out, and_5_out, and_6_out);
  LED led_3 (.in(or_3_out));

  // Notes on the sheet:
  //   S1 = Ta * Tb
  //   S2 = Tb * Tc
  //   S1 = Ta * Tb
  //   S2 = Tb * Tc
  //   S = S1 + S2
  //   S = (Ta * Tb) + (Tb + Tc)
  //   S = S1 + S2
  //   S = (Ta * Tb) + (Tb + Tc)
  //   S1 = Ta * Tb
  //   S2 = Tb * Tc
  //   Resposta: A. Precisamos que o Tb e mais um outro T esteja ligado para que o terminal seja acionado.
  //   S = S1 + S2
  //   S = (Ta * Tb) + (Tb + Tc)
endmodule
