// Logisim project Desafio 3.circ as structural Verilog: 1 circuit, main circuit main
module main (
  input  D,
  input  C,
  input  T,
  input  F,
  input  D_2,
  input  C_2,
  input  T_2,
  input  F_2,
  input  D_3,
  input  C_3,
  input  T_3,
  input  F_3,
  input  D_4,
  input  C_4,
  input  T_4,
  input  F_4,
  output out_17
);

  wire and_1_out, and_2_out, and_3_out, and_4_out, not_1_out, not_2_out, not_3_out, not_4_out;

  not not_1 (not_1_out, C_2);
  not not_2 (not_2_out, F_3);
  not not_3 (not_3_out, C);
  not not_4 (not_4_out, F);
  and and_1 (and_1_out, D_2, not_1_out, T_2, F_2);
  and and_2 (and_2_out, D_3, C_3, T_3, not_2_out);
  and and_3 (and_3_out, D_4, C_4, T_4, F_4);
  and and_4 (and_4_out, D, not_3_out, T, not_4_out);
  or or_1 (out_17, and_4_out, and_1_out, and_2_out, and_3_out);

  // Notes on the sheet:
  //   S2 = D . !C . T . F
  //   S3 = D . C . T . !F
  //   S4 =  D . C . T . F
  //   S1 = D . !C . T . !F
  //   S = S1 + S2 + S3 + S4
  //   S = (D . !C . T . !F) + (D . !C . T . F) + (D . C . T .!F) + (D . C . T .F)
endmodule
