// Logisim project Aula 09-05 Desafio 2 Ex 1 e 2.circ as structural Verilog: 1 circuit, main circuit main
module main (
  input  A,
  input  B,
  input  C,
  input  D,
  input  E,
  input  A_2,
  input  C_2,
  input  D_2,
  input  B_2,
  input  E_2,
  input  F
);

  wire and_1_out, and_2_out, and_3_out, and_4_out, and_5_out, and_6_out, or_1_out;

  and and_1 (and_1_out, A, B, C);
  and and_2 (and_2_out, D, E);
  and and_3 (and_3_out, A_2, C_2);
  and and_4 (and_4_out, D_2, B_2);
  and and_5 (and_5_out, E_2, F);
  and and_6 (and_6_out, and_1_out, and_2_out);
  LED led_1 (.in(and_6_out));
  or or_1 (or_1_out, and_3_out, and_4_out);
  LED led_2 (.in(or_1_out));

  // Notes on the sheet:
  //   S2 = D * E
  //   S1 = A*C
  //   B+D
  //   S2 = 
  //   S3 = F * E
  //   S1 = A * B * C
  //   S = S1 * S2
  //   S = (A * B * C) * ( D +*E)
  //   S = S1 + S2 + S3
endmodule
